# Fritzing sketch schema-final (saved by Fritzing 0.9.3b)
breadboards: 1

parts:
  Composant1 = Arduino Uno (Rev3)
  R1 = Resistor [tolerance=±5% resistance=10k package=THT]
  D1 = Rectifier Diode [part_number=1N4148 package="300 mil [THT]"]
  U1 = LM124-324 Quad Opamp [package="DIP (Dual Inline)"]
  VCC1 = Battery block 9V
  VCC2 = Battery block 9V
  R2 = Resistor [tolerance=±5% resistance=10k package=THT]
  R3 = Resistor [tolerance=±5% resistance=40k package=THT]
  J1 = Peltier Element
  Q1 = MOSFET-NCHANNEL [package=to220v]
  RHT1 = Humidity and Temperature Sensor RHT03  # not connected
  R4 = Resistor [tolerance=±5% resistance=220 package=THT]

nets:
  N1: Composant1.A0, U1.3OUT, R3.Pin_0
  N2: Composant1.GND, D1.cathode, Q1.S, R4.Pin_0
  N3: Composant1.D3_PWM, Q1.G, R4.Pin_1
  N4: Composant1.5V, R1.Pin_1, J1.pin2
  N5: R1.Pin_0, D1.anode, U1.3IN+
  N6: U1.VCC+, VCC1.+
  N7: U1.3IN-, R2.Pin_0, R3.Pin_1
  N8: U1.VCC-, VCC2.-
  N9: VCC1.-, VCC2.+, R2.Pin_1
  N10: J1.pin1, Q1.D
